// Logisim project mac.circ as structural Verilog: 3 circuits, main circuit main
module main (
);

  wire clk, comparator_1_eq, not_1_out, ram_en, rd_mem, rst;
  wire [2:0] sel_mac, sel_op;
  wire [4:0] rgb_video_1_p4, rgb_video_1_p5;
  wire [7:0] rom_img_data;
  wire [9:0] counter_3_q;
  wire [15:0] counter_1_q, ld_a_0, ld_a_1, ld_a_2, ld_a_3, ld_a_4, ld_a_5, ld_a_6, ld_a_7, ld_b_0, ld_b_1,
       ld_b_2, ld_b_3, ld_b_4, ld_b_5, ld_b_6, ld_b_7, op0, op1, op2, op3, op4, op5, op6, op7, w0, w1, w2,
       w3, w4, w5, w6, w7;
  wire [31:0] data_bus, ram_64k_32_dout, random_input_1_random_number;

  // Probe on ld_b_0
  // Probe on ld_a_0
  // Probe on ld_b_4
  // Probe on ld_a_4
  // DipSwitch #(.number(2)) switch: pin names not known; wires that end beside it: rd_mem, ram_en, 1'b1
  Button u_rst (.out(rst));
  Clock clock_1 (.out(clk));
  mac mac_0 (.a(ld_a_0), .b(ld_b_0), .clk(clk), .rst(rst), .op(op0));
  mac mac_4 (.a(ld_a_4), .b(ld_b_4), .clk(clk), .rst(rst), .op(op4));
  Counter #(.max('hffff), .width(16)) counter_1 (
    .load(1'b0), .D({16{1'b0}}), .count(1'b1), .Q(counter_1_q), .up(1'b1), .clk(clk), .clr(rst));  // open: carry
  not not_1 (not_1_out, rd_mem);
  // Probe on random_input_1_random_number
  random_input random_input_1 (.rst(rst), .clk(clk), .random_number(random_input_1_random_number));
  // Probe on op0
  // Probe on op4
  Multiplexer #(.select(3), .width(32)) multiplexer_1 (
    .in0({w0, op0}), .in1({w1, op1}), .in2({w2, op2}), .in3({w3, op3}), .in4({w4, op4}), .in5({w5, op5}),
    .in6({w6, op6}), .in7({w7, op7}), .out(data_bus), .sel(sel_op));
  // Probe on data_bus
  RAM #(.addrWidth(16), .dataWidth(32)) ram_64k_32 (
    .addr(counter_1_q), .we(not_1_out), .oe(rd_mem), .clk(clk), .din(random_input_1_random_number),
    .dout(ram_64k_32_dout));
  // Probe on ld_b_1
  // Probe on ld_b_5
  // Probe on sel_mac
  // Probe on ld_a_1
  // Probe on ld_a_5
  Demultiplexer #(.select(3), .width(32)) demultiplexer_1 (
    .out0({ld_a_0, ld_b_0}), .out1({ld_a_1, ld_b_1}), .out2({ld_a_2, ld_b_2}), .out3({ld_a_3, ld_b_3}),
    .out4({ld_a_4, ld_b_4}), .out5({ld_a_5, ld_b_5}), .out6({ld_a_6, ld_b_6}), .out7({ld_a_7, ld_b_7}),
    .in(data_bus), .sel(sel_mac));
  // Probe on ram_64k_32_dout[31:16]
  // Probe on ram_64k_32_dout[15:0]
  Counter #(.max('h7), .width(3)) counter_2 (.Q(sel_mac), .clk(clk));  // open: load, D, count, carry, up, clr
  assign data_bus = ram_en ? ram_64k_32_dout : 32'bz;  // Controlled_Buffer controlled_buffer_1
  // Probe on op1
  mac mac_1 (.a(ld_a_1), .b(ld_b_1), .clk(clk), .rst(rst), .op(op1));
  // Probe on op5
  mac mac_5 (.a(ld_a_5), .b(ld_b_5), .clk(clk), .rst(rst), .op(op5));
  // Probe on ld_b_2
  // Probe on ld_b_6
  ROM #(.addrWidth(10)) rom_img (.addr(counter_3_q), .data(rom_img_data));
  // Probe on ld_a_2
  // Probe on ld_a_6
  Counter #(.max('h3ff), .width(10)) counter_3 (
    .Q(counter_3_q), .clk(clk), .clr(rst));  // open: load, D, count, carry, up
  // Probe on op2
  mac mac_2 (.a(ld_a_2), .b(ld_b_2), .clk(clk), .rst(rst), .op(op2));
  // Probe on op6
  mac mac_6 (.a(ld_a_6), .b(ld_b_6), .clk(clk), .rst(rst), .op(op6));
  // Probe on ld_b_3
  // Probe on ld_b_7
  // RGB_Video #(.height(32), .scale(8), .width(32)) rgb_video_1: pin names not known; wires that end beside it: rst, clk, 1'b1, rgb_video_1_p4, rgb_video_1_p5, {{16{1'b0}}, rom_img_data}
  Counter #(.max('h1f), .width(5)) x_cdnt (
    .Q(rgb_video_1_p4), .clk(clk), .clr(rst));  // open: load, D, count, carry, up
  // Probe on ld_a_3
  // Probe on ld_a_7
  Comparator #(.width(5)) comparator_1 (.a(rgb_video_1_p4), .b({5{1'b1}}), .eq(comparator_1_eq));  // open: gt, lt
  Counter #(.max('h1f), .width(5)) y_cdnt (
    .Q(rgb_video_1_p5), .clk(comparator_1_eq), .clr(rst));  // open: load, D, count, carry, up
  // Probe on op3
  mac mac_3 (.a(ld_a_3), .b(ld_b_3), .clk(clk), .rst(rst), .op(op3));
  // Probe on op7
  mac mac_7 (.a(ld_a_7), .b(ld_b_7), .clk(clk), .rst(rst), .op(op7));

  // Notes on the sheet:
  //   contents of rom_img (hex, n*v repeats v):
  //   230*0 54 b9 9f 97 3c 24 26*0 de 4*fe f1 8*c6 aa 34 16*0 43 72 48 72 a3 e3 fe e1 fe fe fe fa e5 fe fe
  //   8c 21*0 11 42 e 43 43 43 3b 15 ec fe 6a 28*0 53 fd d1 12 27*0 16 e9 ff 53 28*0 81 fe ee 2c 27*0 3b
  //   f9 fe 3e 28*0 85 fe bb 5 27*0 9 cd f8 3a 28*0 7e fe b6 28*0 4b fb f0 39 27*0 13 dd fe a6 27*0 3 cb
  //   fe db 23 27*0 26 fe fe 4d 27*0 1f e0 fe 73 1 27*0 85 fe fe 34 27*0 3d f2 fe fe 34 27*0 79 fe fe db
  //   28 27*0 79 fe cf 12
endmodule

module mac (
  input  [15:0] a,
  input  [15:0] b,
  input  clk,
  input  rst,
  output [15:0] op
);

  wire not_1_out;
  wire [15:0] bit_extender_1_out, multiplexer_1_out, multiplexer_2_out, multiplier_1_out;

  assign bit_extender_1_out = {{15{1'b0}}, 1'b0};  // Bit_Extender bit_extender_1
  // Probe on a
  // Probe on b
  Multiplexer #(.width(16)) multiplexer_1 (.in0(bit_extender_1_out), .in1(a), .out(multiplexer_1_out), .sel(not_1_out));
  Multiplexer #(.width(16)) multiplexer_2 (.in0(bit_extender_1_out), .in1(b), .out(multiplexer_2_out), .sel(not_1_out));
  not not_1 (not_1_out, rst);
  // Probe on multiplier_1_out
  Multiplier #(.width(16)) multiplier_1 (
    .a(multiplexer_1_out), .b(multiplexer_2_out), .out(multiplier_1_out), .cin(op));  // open: cout
  // Probe on op
  Register #(.width(16)) register_1 (.D(multiplier_1_out), .en(1'b1), .clk(clk), .Q(op), .clr(rst));
endmodule

module random_input (
  input  rst,
  input  clk,
  output [31:0] random_number
);

  wire random_1_out;

  Random #(.width(1)) random_1 (.clk(clk), .out(random_1_out));  // open: clr, next
  Random random_2 (.clr(rst), .next(random_1_out), .clk(clk), .out(random_number[7:0]));
  Random random_3 (.clr(rst), .clk(clk), .out(random_number[23:16]));  // open: next
  // Probe on random_number[7:0]
  // Probe on random_number[23:16]
  // Probe on {{8{1'b0}}, random_number[7:0]}
  // Probe on {{8{1'b0}}, random_number[23:16]}
  // Probe on {{8{1'b0}}, random_number[23:16], {8{1'b0}}, random_number[7:0]}

  assign {random_number[31:24], random_number[15:8]} = {16{1'b0}};
endmodule
